// Logisim project FULL ADDER USING NAND GATES.circ as structural Verilog: 2 circuits, main circuit main
module main (
  input  A,
  input  B,
  input  C,
  output out_4,
  output out_5
);

  wire nand_1_out, nand_2_out, nand_3_out, nand_4_out, nand_5_out, nand_6_out, nand_7_out;

  nand nand_1 (nand_1_out, A, B);
  nand nand_2 (nand_2_out, A, nand_1_out);
  nand nand_3 (nand_3_out, nand_1_out, B, B);
  nand nand_4 (nand_4_out, nand_2_out, nand_3_out);
  nand nand_5 (nand_5_out, nand_4_out, C);
  nand nand_6 (nand_6_out, nand_4_out, nand_5_out);
  nand nand_7 (nand_7_out, nand_5_out, C, C);
  nand nand_8 (out_5, nand_5_out, nand_1_out);
  nand nand_9 (out_4, nand_6_out, nand_7_out);

  // Notes on the sheet:
  //   FULL ADDER USING NAND GATES
  //   (A.B)
  //   A+B
  //   S=A+B+C
endmodule

module NAND (
  input  a,
  input  b,
  input  c,
  output x,
  output y
);

  wire nand_1_out, nand_2_out, nand_3_out, nand_4_out, nand_5_out, nand_6_out, nand_7_out, nand_8_out,
       nand_9_out, nand_10_out, nand_11_out, nand_12_out, nand_13_out;

  nand nand_1 (nand_1_out, a, a);
  nand nand_2 (nand_2_out, b, b);
  nand nand_3 (nand_3_out, a, a);
  nand nand_4 (nand_4_out, c, c);
  nand nand_5 (nand_5_out, b, b);
  nand nand_6 (nand_6_out, c, c);
  nand nand_7 (nand_7_out, b, c);
  nand nand_8 (nand_8_out, a, c);
  nand nand_9 (nand_9_out, a, b);
  nand nand_10 (nand_10_out, nand_1_out, nand_2_out, c);
  nand nand_11 (nand_11_out, nand_3_out, b, nand_4_out);
  nand nand_12 (nand_12_out, a, nand_5_out, nand_6_out);
  nand nand_13 (nand_13_out, a, b, c);
  nand nand_14 (y, nand_7_out, nand_8_out, nand_9_out);
  nand nand_15 (x, nand_10_out, nand_11_out, nand_12_out, nand_13_out);
endmodule
